# Fritzing sketch firstCircuits-twoLEDs (saved by Fritzing 0.9.4)
breadboards: 1

parts:
  Part1 = Arduino Uno (Rev3) - ICSP
  R1 = Resistor [tolerance=±5% resistance=1k package=THT]
  R2 = Resistor [tolerance=±5% resistance=1k package=THT]
  LED2 = smd LED [color="Red (633nm)" package="0603 [SMD]"]
  LED3 = smd LED [color="Red (633nm)" package="0603 [SMD]"]

nets:
  N1: Part1.5V, R2.Pin_1, LED2.anode
  N2: Part1.GND, R1.Pin_0, LED3.cathode
  N3: R1.Pin_1, LED2.cathode
  N4: R2.Pin_0, LED3.anode
